# Fritzing sketch FF_LivingRoom_v10 (saved by Fritzing 0.9.2b)

parts:
  U1 = ESP8266 WiFi Module [part_number=ESP8266]
  U4 = Voltage Regulator [package=to220-adj]
  J1 = Power Jack [package=power_jack_combo]
  JP1 = FTDI_BASIC [package=ftdi_basic]

nets:
  N1: U1.VCC, U1.GPIO_2, U1.CH_PD, U4.OUT
  GND: U1.GPIO_0, U1.GND, U1.GPIO_15, U4.ADJ, J1.GND
  N2: U1.GPIO_4, JP1.1
  N3: U1.GPIO_5, JP1.6
  N4: U1.GPIO_12, JP1.5
  N5: U4.IN, J1.PWR

custom parts:
  ESP8266 WiFi Module: Generic WiFi Module based on the ESP8266 with onboard PCB antenna and UART communications
  Voltage Regulator: Voltage Regulator Standard ASM1117 adjustable voltage regulator.
