# Fritzing sketch domus-silicea-board1-2 (saved by Fritzing 0.9.2b)

parts:
  Componente1 = Arduino Pro Mini v13
  DHT1 = DHT11 Humitidy and Temperature Sensor
  IR1 = TSOP312.., 314.. [part_number=TSOP38238 package=THT]
  Q1 = TRANSISTOR_NPN [part_number=P2N2222AGOD-ND package=to-92]
  D1 = LTE-302 [part_number="940nm IR LEDs" package=lte-302]
  R2 = Resistor [tolerance=±5% resistance=0 package=THT]
  R3 = Resistor [tolerance=±5% resistance=220 package=THT]
  VCC1 = Battery
  NRF24L1 = NRF24L01

nets:
  3.3V: Componente1.VCC, DHT1.VDD, IR1.Vs, R2.Pin_1, VCC1.+, NRF24L1.VCC
  GND: Componente1.GND, DHT1.GND, IR1.GND, Q1.E, VCC1.-, NRF24L1.GND
  N1: Componente1.D13/SCK, NRF24L1.SCK
  N2: Componente1.D12/MISO, NRF24L1.MISO
  N3: Componente1.D11_PWM/MOSI, NRF24L1.MOSI
  N4: Componente1.D10_PWM/SS, NRF24L1.CSN
  N5: Componente1.D9_PWM, NRF24L1.CE
  N6: Componente1.D8, DHT1.DATA
  N7: Componente1.D7, IR1.Data
  N8: Componente1.D6_PWM, R3.Pin_0
  N9: Q1.B, R3.Pin_1
  N10: Q1.C, D1.C
  N11: D1.A, R2.Pin_0

custom parts:
  DHT11 Humitidy and Temperature Sensor: DHT11 Humidity and Temperature Sensor
  NRF24L01: NRF24L01 module
