# Fritzing sketch domus-silicea-board1-3 (saved by Fritzing 0.9.2b)

parts:
  Componente1 = Arduino Pro Mini v13
  DHT1 = DHT11 Humitidy and Temperature Sensor
  IR1 = TSOP312.., 314.. [part_number=TSOP38238 package=THT]
  Q1 = TRANSISTOR_NPN [part_number=P2N2222AGOD-ND package=to-92]
  D1 = LTE-302 [part_number="940nm IR LEDs" package=lte-302]
  R2 = Resistor [tolerance=±5% resistance=0 package=THT]
  R3 = Resistor [tolerance=±5% resistance=220 package=THT]
  VCC1 = Battery
  NRF24L1 = NRF24L01
  HC-SR1 = HC-SR04
  PIR1 = PIR sensor
  R4 = Resistor [tolerance=±5% resistance=1M package=THT]
  S2 = SWITCH-MOMENTARY-2 [package=reed_switch_pth]

nets:
  3.3V: Componente1.VCC, DHT1.VDD, IR1.Vs, R2.Pin_1, VCC1.+, NRF24L1.VCC, HC-SR1.VCC, PIR1.VDD, R4.Pin_0
  GND: Componente1.GND, DHT1.GND, IR1.GND, Q1.E, VCC1.-, NRF24L1.GND, HC-SR1.GND, PIR1.GND, S2.2
  N1: Componente1.A1, HC-SR1.Trig
  N2: Componente1.D13/SCK, NRF24L1.SCK
  N3: Componente1.D12/MISO, NRF24L1.MISO
  N4: Componente1.D11_PWM/MOSI, NRF24L1.MOSI
  N5: Componente1.D10_PWM/SS, NRF24L1.CSN
  N6: Componente1.D9_PWM, NRF24L1.CE
  N7: Componente1.D8, DHT1.DATA
  N8: Componente1.D7, IR1.Data
  N9: Componente1.D6_PWM, R3.Pin_0
  N10: Componente1.D5_PWM, R4.Pin_1, S2.1
  N11: Componente1.D4, PIR1.SIG
  N12: Q1.B, R3.Pin_1
  N13: Q1.C, D1.C
  N14: D1.A, R2.Pin_0

custom parts:
  DHT11 Humitidy and Temperature Sensor: DHT11 Humidity and Temperature Sensor
  NRF24L01: NRF24L01 module
  HC-SR04: Parallax Ping
