# Fritzing sketch domus-silicea-board1-5 (saved by Fritzing 0.9.2b)

parts:
  Arduino_Pro_Mini_3_3V = Arduino Pro Mini v13
  DHT1 = DHT11 Humitidy and Temperature Sensor
  IR1 = TSOP312.., 314.. [part_number=TSOP38238 package=THT]
  Q1 = TRANSISTOR_NPN [part_number=P2N2222AGOD-ND package=to-92]
  D1 = LTE-302 [part_number="940nm IR LEDs" package=lte-302]
  R2 = Resistor [tolerance=±5% resistance=0 package=THT]
  R3 = Resistor [tolerance=±5% resistance=220 package=THT]
  VCC1 = Battery
  PIR1 = PIR sensor
  R4 = Resistor [tolerance=±5% resistance=1M package=THT]
  S2 = SWITCH-MOMENTARY-2 [package=reed_switch_pth]
  HC-SR2 = HC-SR04
  NRF24L3 = NRF24L01
  J2 = female pin header, 3 pins [form="♀ (female)"]

nets:
  3.3V: Arduino_Pro_Mini_3_3V.VCC, DHT1.VDD, IR1.Vs, R2.Pin_1, VCC1.+, PIR1.VDD, R4.Pin_0, HC-SR2.VCC, NRF24L3.VCC, J2.pin2
  GND: Arduino_Pro_Mini_3_3V.GND, DHT1.GND, IR1.GND, Q1.E, VCC1.-, PIR1.GND, S2.2, HC-SR2.GND, NRF24L3.GND, J2.pin3
  5V: Arduino_Pro_Mini_3_3V.RAW, J2.pin1
  nRF24_IRQ: Arduino_Pro_Mini_3_3V.A2, NRF24L3.IRQ
  PING_TX: Arduino_Pro_Mini_3_3V.A1, HC-SR2.Trig
  PING_RX: Arduino_Pro_Mini_3_3V.A0, HC-SR2.Echo
  nRF24_SCK: Arduino_Pro_Mini_3_3V.D13/SCK, NRF24L3.SCK
  nRF24_MISO: Arduino_Pro_Mini_3_3V.D12/MISO, NRF24L3.MISO
  nRF24_MOSI: Arduino_Pro_Mini_3_3V.D11_PWM/MOSI, NRF24L3.MOSI
  nRF24_CSN: Arduino_Pro_Mini_3_3V.D10_PWM/SS, NRF24L3.CSN
  nRF24_CE: Arduino_Pro_Mini_3_3V.D9_PWM, NRF24L3.CE
  DHT_DATA: Arduino_Pro_Mini_3_3V.D8, DHT1.DATA
  IR_RX: Arduino_Pro_Mini_3_3V.D7, IR1.Data
  IR_TX: Arduino_Pro_Mini_3_3V.D6_PWM, R3.Pin_0
  SWITCH: Arduino_Pro_Mini_3_3V.D5_PWM, R4.Pin_1, S2.1
  PIR_DATA: Arduino_Pro_Mini_3_3V.D4, PIR1.SIG
  N1: Q1.B, R3.Pin_1
  N2: Q1.C, D1.C
  N3: D1.A, R2.Pin_0

custom parts:
  DHT11 Humitidy and Temperature Sensor: DHT11 Humidity and Temperature Sensor
  HC-SR04: Parallax Ping
  NRF24L01: NRF24L01 module
