# Fritzing sketch domus-silicea-board2-1 (saved by Fritzing 0.9.2b)
breadboards: 1

parts:
  PIR1 = HC-SR501 PIR Sensor
  DHT = Humidity and Temperature Sensor RHT03
  R1 = Resistor [tolerance=±5% resistance=10k package=THT]
  U1 = atmega328 [package=dip]
  RESET = Pushbutton [package="[THT]"]
  3v3 = Battery
  IR2 = TSOP312.., 314.. [package=THT]
  IR1 = LED - 5mm [color="Infrared (940nm)" package="5 mm [THT]"]  # not connected
  LED1 = LED - 5mm [color="Red (633nm)" package="5 mm [THT]"]  # not connected
  Q1 = NPN-Transistor [package="TO92 [THT]"]  # not connected
  D1 = Rectifier Diode [part_number=1N4001 package="300 mil [THT]"]  # not connected
  XTAL1 = Crystal [frequency="8 MHz" package=THT]  # not connected
  NRF24L1 = NRF24L01
  FTDI = IC, SIP package, 6 pins [chip_label=FTDI part_number=FTDI]  # not connected

nets:
  GND: PIR1.GND, DHT.GND_1, DHT.GND_2, U1.GND, 3v3.-, IR2.GND, NRF24L1.GND
  VCC: PIR1.TRG, PIR1.+3V3, DHT.Vcc, R1.Pin_0, U1.VCC, U1.AVCC, 3v3.+, IR2.Vs, NRF24L1.VCC
  N1: DHT.Data-signal, R1.Pin_1
  N2: U1.RESET, RESET.Pin_1, RESET.Pin_2
  N3: RESET.Pin_3, RESET.Pin_4

custom parts:
  NRF24L01: NRF24L01 module
