# Fritzing sketch domus-silicea-board3-3 (saved by Fritzing 0.9.2b)
circuit board: 6cm x 5cm

parts:
  Pro_Mini = Arduino Pro Mini v13
  NRF24L1 = NRF24L01
  DHT = Humidity and Temperature Sensor RHT03
  PIR1 = HC-SR501 PIR Sensor
  LED1 = LED - 5mm [color="Infrared (940nm)" package="5 mm [THT]"]
  Q1 = NPN-Transistor [package="TO92 [THT]"]
  R1 = Resistor [tolerance=±5% resistance=220 package=THT]
  IR1 = TSOP312.., 314.. [package=THT]
  C1 = Electrolytic Capacitor [capacitance=1µF package="100 mil [THT, electrolytic]"]
  R2 = Resistor [tolerance=±5% resistance=10k package=THT]
  R3 = Resistor [tolerance=±5% resistance=10k package=THT]
  R4 = Resistor [tolerance=±5% resistance=0 package=THT]
  BAT = Battery
  S1 = Reed switch [package=THT]
  R5 = Resistor [tolerance=±5% resistance=220 package=THT]
  ESP01 = ESP8266 WiFi Module [part_number=ESP8266]

nets:
  VCC: Pro_Mini.VCC, NRF24L1.VCC, DHT.Vcc, PIR1.TRG, PIR1.+3V3, IR1.Data, C1.+, R2.Pin_0, R3.Pin_0, R4.Pin_1, BAT.+, R5.Pin_1, ESP01.VCC, ESP01.CH_PD
  GND: Pro_Mini.GND, NRF24L1.GND, DHT.GND_2, PIR1.GND, PIR1.GND2, Q1.E, IR1.Vs, BAT.-, S1.pin_2, ESP01.GND
  N1: Pro_Mini.D13/SCK, NRF24L1.SCK
  N2: Pro_Mini.D12/MISO, NRF24L1.MISO
  N3: Pro_Mini.D11_PWM/MOSI, NRF24L1.MOSI
  N4: Pro_Mini.D10_PWM/SS, NRF24L1.CSN
  N5: Pro_Mini.D9_PWM, NRF24L1.CE
  N6: Pro_Mini.D8, DHT.Data-signal, R2.Pin_1
  N7: Pro_Mini.D7, IR1.GND
  N8: Pro_Mini.D6_PWM, R1.Pin_0
  N9: Pro_Mini.D3_PWM, S1.pin_1, R5.Pin_0
  N10: Pro_Mini.D2, PIR1.SIG, R3.Pin_1
  N11: Pro_Mini.D1/RX, ESP01.TXD
  N12: Pro_Mini.D0/TX, ESP01.RXD
  N13: LED1.cathode, Q1.C
  N14: LED1.anode, R4.Pin_0
  N15: Q1.B, R1.Pin_1

notes:
  ir is different
  capacitor to conf

custom parts:
  NRF24L01: NRF24L01 module
  ESP8266 WiFi Module: Generic WiFi Module based on the ESP8266 with onboard PCB antenna and UART communications
