# Fritzing sketch domus-silicea-photodiode-1 (saved by Fritzing 0.9.2b)
breadboards: 1

parts:
  P1 = S1133 Si Photodiode [package="8mm Ceramic [THT]"]
  U1 = IC, DIP package, 14 pins [chip_label=TS27L4]
  Part1 = Arduino Uno (Rev3)
  R1 = Resistor [tolerance=±5% resistance=100k package="1206 [SMD]"]
  R2 = Resistor [tolerance=±5% resistance=100k package="1206 [SMD]"]
  R3 = Resistor [tolerance=±5% resistance=270 package=THT]

nets:
  N1: P1.cathode, U1.pin3, U1.pin11, Part1.GND, R3.Pin_1
  N2: P1.anode, U1.pin2, R1.Pin_1
  N3: U1.pin1, U1.pin5, R1.Pin_0
  N4: U1.pin4, Part1.5V
  N5: U1.pin6, R2.Pin_0, R3.Pin_0
  N6: U1.pin7, Part1.D2, R2.Pin_1

notes:
  100k
  270
