# Fritzing sketch nodemcu-arduinopromini (saved by Fritzing 0.9.2b)

parts:
  U1 = NodeMCU V1.0
  Part1 = Arduino Pro Mini v13
  U2 = NodeMCU V1.0
  Part2 = Arduino Pro Mini v13
  U3 = ESP8266 WiFi Module [part_number=ESP8266]
  Part3 = Arduino Pro Mini v13
  R1 = Resistor [tolerance=±5% resistance=4.7k package=THT]
  R2 = Resistor [tolerance=±5% resistance=4.7k package=THT]

nets:
  GND: U1.GND, Part1.GND
  N1: U1.CLK, Part1.D13/SCK
  N2: U1.SD0, Part1.D11_PWM/MOSI
  N3: U1.SD1, Part1.D12/MISO
  N4: U1.SD2, Part1.D10_PWM/SS
  N5: U2.D4, Part2.D2
  GND_2: U2.GND, Part2.GND
  N6: Part2.VCC, R2.Pin_0
  N7: Part2.D12/MISO, R2.Pin_1
  N8: U3.GPIO_2, Part3.D2, R1.Pin_1
  N9: Part3.VCC, R1.Pin_0

notes:
  GND (to flash)
  CH_PD (VCC)
  RX -->
  <-- TX

custom parts:
  NodeMCU V1.0: ESP9266 based NodeMCU
  ESP8266 WiFi Module: Generic WiFi Module based on the ESP8266 with onboard PCB antenna and UART communications
